# Fritzing sketch CIRCUIT_SKETCH (saved by Fritzing 0.9.4)
breadboards: 2

parts:
  ARD02 = Arduino Uno (Rev3)
  ARD01 = Arduino Uno (Rev3)
  R1 = Resistor [tolerance=±5% resistance=10k package="2512 [SMD]"]
  R2 = Resistor [tolerance=±5% resistance=10k package="2512 [SMD]"]
  LED1 = smd LED [color="Red (633nm)" package="0805 [SMD]"]
  LED2 = smd LED [color="Green (560nm)" package="0805 [SMD]"]
  R6 = Resistor [tolerance=±5% resistance=220 package="2512 [SMD]"]
  R7 = Resistor [tolerance=±5% resistance=220 package="2512 [SMD]"]
  BLUE_SWITCH = Pushbutton [package=THT]
  YELLOW_SWITCH = Pushbutton [package=THT]
  CHAMBER_LED = Round Pushbutton
  CURRENT_GENERATOR = Round Pushbutton
  TONE_GENERATOR = Round Pushbutton
  D1 = Rectifier Diode [part_number=1N4001 package="300 mil [THT]"]
  GREEN_BUTTON = Pushbutton [package=THT]
  R8 = Resistor [tolerance=±5% resistance=10k package="2512 [SMD]"]

nets:
  N1: ARD02.D8, CURRENT_GENERATOR.leg0
  N2: ARD02.D9_PWM, CHAMBER_LED.leg0
  N3: ARD02.D11_PWM/MOSI, LED2.anode
  N4: ARD02.D12/MISO, LED1.anode
  N5: ARD02.D13/SCK, D1.anode
  N6: ARD02.D2, R1.Pin_1, BLUE_SWITCH.leg1
  N7: ARD02.D3_PWM, R2.Pin_1, YELLOW_SWITCH.leg1
  N8: ARD02.D7, TONE_GENERATOR.leg0
  N9: ARD02.5V, BLUE_SWITCH.leg0, YELLOW_SWITCH.leg0
  N10: ARD02.GND, R1.Pin_0, R2.Pin_0, R6.Pin_0, R7.Pin_0, CHAMBER_LED.leg1, CURRENT_GENERATOR.leg1, TONE_GENERATOR.leg1
  N11: ARD01.D2, D1.cathode, GREEN_BUTTON.leg1, R8.Pin_0
  N12: LED1.cathode, R6.Pin_1
  N13: LED2.cathode, R7.Pin_1
