# Fritzing sketch CIRCUIT_SKETCH (saved by Fritzing 0.9.4)
breadboards: 2

parts:
  ARD02 = Arduino Uno (Rev3)
  ARD01 = Arduino Uno (Rev3)
  R1 = Resistor [tolerance=±5% resistance=10k package="2512 [SMD]"]
  R2 = Resistor [tolerance=±5% resistance=10k package="2512 [SMD]"]
  LED1 = smd LED [color="Red (633nm)" package="0805 [SMD]"]
  LED2 = smd LED [color="Green (560nm)" package="0805 [SMD]"]
  R6 = Resistor [tolerance=±5% resistance=220 package="2512 [SMD]"]
  R7 = Resistor [tolerance=±5% resistance=220 package="2512 [SMD]"]
  BLUE_SWITCH = Pushbutton [package=THT]
  YELLOW_SWITCH = Pushbutton [package=THT]
  CURRENT_GENERATOR = Round Pushbutton
  TONE_GENERATOR = Round Pushbutton
  D1 = Rectifier Diode [part_number=1N4001 package="300 mil [THT]"]
  GREEN_BUTTON = Pushbutton [package=THT]
  R8 = Resistor [tolerance=±5% resistance=10k package="2512 [SMD]"]
  R9 = Resistor [tolerance=±5% resistance=10k package="2512 [SMD]"]
  R10 = Resistor [tolerance=±5% resistance=220 package="2512 [SMD]"]
  FOOD_MAGAZINE = Stepper Motor - Bipolar
  S1 = H-Bridge with L298N
  Power1 = PowerBRICK 12V
  CHAMBER_LEVER = Round Pushbutton
  Food_Tray_LED = smd LED [color="Green (555nm)" package="0805 [SMD]"]
  CHAMBER_LEDs = smd LED [color="Infrared (940nm)" package="0805 [SMD]"]

nets:
  N1: ARD02.D8, CURRENT_GENERATOR.leg0
  N2: ARD02.D9_PWM, CHAMBER_LEDs.cathode
  N3: ARD02.D11_PWM/MOSI, LED2.anode
  N4: ARD02.D12/MISO, LED1.anode
  N5: ARD02.D13/SCK, D1.anode
  N6: ARD02.D2, R1.Pin_1, BLUE_SWITCH.leg1
  N7: ARD02.D3_PWM, R2.Pin_1, YELLOW_SWITCH.leg1
  N8: ARD02.D7, TONE_GENERATOR.leg0
  N9: ARD02.5V, BLUE_SWITCH.leg0, YELLOW_SWITCH.leg0
  N10: ARD02.GND, R1.Pin_0, R2.Pin_0, R6.Pin_0, R7.Pin_0, CURRENT_GENERATOR.leg1, TONE_GENERATOR.leg1, CHAMBER_LEDs.anode
  N11: ARD01.D8, Food_Tray_LED.anode
  N12: ARD01.D9_PWM, R9.Pin_0, CHAMBER_LEVER.leg1
  N13: ARD01.D2, D1.cathode, GREEN_BUTTON.leg1, R8.Pin_0
  5V: ARD01.5V, GREEN_BUTTON.leg0, S1.5V, CHAMBER_LEVER.leg0
  GND: ARD01.GND, R8.Pin_1, R9.Pin_1, R10.Pin_1, S1.GND, Power1.GND
  N14: LED1.cathode, R6.Pin_1
  N15: LED2.cathode, R7.Pin_1
  N16: R10.Pin_0, Food_Tray_LED.cathode
  N17: FOOD_MAGAZINE.A, S1.M1-01
  N18: FOOD_MAGAZINE.C, S1.M1-02
  N19: FOOD_MAGAZINE.B, S1.M2-02
  N20: FOOD_MAGAZINE.D, S1.M2-01
  N21: S1.12V, Power1.+Vout

custom parts:
  H-Bridge with L298N: h-bridge
  PowerBRICK 12V: PowerBRICKs are split-rail power supply modules that are intended to be used with a breadboard. These generate both a negative and positive voltage out of a single 5V USB voltage.
